# Fritzing sketch schema (saved by Fritzing 0.9.0b)
breadboards: 1

parts:
  Part1 = Rotoshield - Motor driver shield for Arduino
  U1 = MLX90614 [package=to-39]
  C2 = Tantalum Capacitor [capacitance=1μF package="100 mil [THT, tantalum]"]
  R1 = Resistor [tolerance=±5% resistance=4.7k package=THT]
  R2 = Resistor [tolerance=±5% resistance=4.7k package=THT]
  M1 = Stepper Motor - Bipolar
  M2 = Stepper Motor - Bipolar
  S1 = Toggle Switch [package=THT]
  R3 = Resistor [tolerance=±5% resistance=10k package=THT]
  R4 = Resistor [tolerance=±5% resistance=10k package=THT]
  S2 = Toggle Switch [package=THT]
  LED1 = LED - 5mm [color="Red (633nm)" package="5 mm [THT]"]

nets:
  N1: Part1.A_IN_4, U1.PWM_SDA, R1.Pin_1
  N2: Part1.A_IN_5, U1.SCL_VZ, R2.Pin_1
  N3: Part1.DIG_10, R4.Pin_0
  N4: Part1.DIG_11, S1.L1, R3.Pin_0
  N5: Part1.DIG_12, LED1.anode
  +3V3: Part1.+3V3, U1.VDD, C2.+
  N6: Part1.+5V, S1.L2, S2.L2, LED1.cathode
  GND: Part1.GND, U1.VSS, C2.-, R3.Pin_1, R4.Pin_1
  N7: Part1.M1-2, M2.C
  N8: Part1.M1-1, M2.A
  N9: Part1.M2-2, M2.D
  N10: Part1.M2-1, M2.B
  N11: Part1.M3-2, M1.C
  N12: Part1.M3-1, M1.A
  N13: Part1.M4-2, M1.D
  N14: Part1.M4-1, M1.B
  N15: R1.Pin_0, R2.Pin_0

notes:
  small laser beam -
  DON'T LOOK AT LASER WITH REMAINING EYES!!!
  MLX 90614ESF-DCI
  mechanical end stop
